// Logisim project Decade up-down counter.circ as structural Verilog: 1 circuit, main circuit main
module main (
  input  SD,
  input  SD_2,
  input  SD_3,
  input  SD_4,
  input  Enable,
  input  Enable_2,
  input  Enable_3,
  input  Enable_4,
  input  RD,
  input  RD_2,
  input  RD_3,
  input  RD_4,
  output Q3,
  output Q2,
  output Q1,
  output Q0,
  output Q3_2,
  output Q2_2,
  output Q1_2,
  output Q0_2,
  output Q3_3,
  output Q2_3,
  output Q1_3,
  output Q0_3,
  output Q3_4,
  output Q2_4,
  output Q1_4,
  output Q0_4,
  output D1,
  output D0,
  output D1_2,
  output D0_2,
  output D1_3,
  output D0_3,
  output D1_4,
  output D0_4,
  output D3,
  output D2,
  output D3_2,
  output D2_2,
  output D3_3,
  output D2_3,
  output D3_4,
  output D2_4
);

  wire button_1_out, button_2_out, button_3_out, button_4_out, nor_1_out, not_1_out, not_2_out, not_3_out,
       not_4_out, not_5_out, not_6_out, not_7_out;

  Button button_1 (.out(button_1_out));
  not not_1 (not_1_out, Q2);
  D_Flip_Flop d_ff_1 (.clk(button_1_out), .D(D3), .Q(Q3), .preset(SD), .en(Enable), .reset(RD));  // open: Qn
  Multiplexer #(.select(2)) multiplexer_1 (
    .in0(Q3), .in1(1'b0), .in2(1'b0), .in3(Q2), .out(D3), .sel({Q1, Q0}));  // open: en
  Multiplexer #(.select(2)) multiplexer_2 (
    .in0(Q2), .in1(Q2), .in2(Q2), .in3(not_1_out), .out(D2), .sel({Q1, Q0}));  // open: en
  D_Flip_Flop d_ff_2 (.clk(button_1_out), .D(D2), .Q(Q2), .preset(SD), .en(Enable), .reset(RD));  // open: Qn
  not not_2 (not_2_out, Q3);
  D_Flip_Flop d_ff_3 (.clk(button_1_out), .D(D1), .Q(Q1), .preset(SD), .en(Enable), .reset(RD));  // open: Qn
  Multiplexer #(.select(2)) multiplexer_3 (
    .in0(1'b0), .in1(not_2_out), .in2(1'b1), .in3(1'b0), .out(D1), .sel({Q1, Q0}));  // open: en
  Multiplexer #(.select(2)) multiplexer_4 (
    .in0(1'b1), .in1(1'b0), .in2(1'b1), .in3(1'b0), .out(D0), .sel({Q1, Q0}));  // open: en
  D_Flip_Flop d_ff_4 (.clk(button_1_out), .D(D0), .Q(Q0), .preset(SD), .en(Enable), .reset(RD));  // open: Qn
  Button button_2 (.out(button_2_out));
  nor nor_1 (nor_1_out, Q3_2, Q2_2);
  D_Flip_Flop d_ff_5 (.clk(button_2_out), .D(D3_2), .Q(Q3_2), .preset(SD_2), .en(Enable_2), .reset(RD_2));  // open: Qn
  Multiplexer #(.select(2)) multiplexer_5 (
    .in0(nor_1_out), .in1(Q3_2), .in2(1'b0), .in3(1'b0), .out(D3_2), .sel({Q1_2, Q0_2}));  // open: en
  Multiplexer #(.select(2)) multiplexer_6 (
    .in0(Q3_2), .in1(Q2_2), .in2(Q2_2), .in3(Q2_2), .out(D2_2), .sel({Q1_2, Q0_2}));  // open: en
  D_Flip_Flop d_ff_6 (.clk(button_2_out), .D(D2_2), .Q(Q2_2), .preset(SD_2), .en(Enable_2), .reset(RD_2));  // open: Qn
  D_Flip_Flop d_ff_7 (.clk(button_2_out), .D(D1_2), .Q(Q1_2), .preset(SD_2), .en(Enable_2), .reset(RD_2));  // open: Qn
  not not_3 (not_3_out, nor_1_out);
  Multiplexer #(.select(2)) multiplexer_7 (
    .in0(not_3_out), .in1(1'b0), .in2(1'b0), .in3(1'b1), .out(D1_2), .sel({Q1_2, Q0_2}));  // open: en
  Multiplexer #(.select(2)) multiplexer_8 (
    .in0(1'b1), .in1(1'b0), .in2(1'b1), .in3(1'b0), .out(D0_2), .sel({Q1_2, Q0_2}));  // open: en
  D_Flip_Flop d_ff_8 (.clk(button_2_out), .D(D0_2), .Q(Q0_2), .preset(SD_2), .en(Enable_2), .reset(RD_2));  // open: Qn
  Button button_3 (.out(button_3_out));
  D_Flip_Flop d_ff_9 (.clk(button_3_out), .D(D3_3), .Q(Q3_3), .preset(SD_3), .en(Enable_3), .reset(RD_3));  // open: Qn
  Multiplexer #(.select(2)) multiplexer_9 (
    .in0(not_5_out), .in1(1'b1), .in2(1'b0), .in3(1'b0), .out(D3_3), .sel({Q1_3, Q0_3}));  // open: en
  Multiplexer #(.select(2)) multiplexer_10 (
    .in0(1'b1), .in1(1'b0), .in2(1'b0), .in3(1'b0), .out(D2_3), .sel({Q1_3, Q0_3}));  // open: en
  not not_4 (not_4_out, Q3_3);
  D_Flip_Flop d_ff_10 (.clk(button_3_out), .D(D2_3), .Q(Q2_3), .preset(SD_3), .en(Enable_3), .reset(RD_3));  // open: Qn
  not not_5 (not_5_out, Q2_3);
  D_Flip_Flop d_ff_11 (.clk(button_3_out), .D(D1_3), .Q(Q1_3), .preset(SD_3), .en(Enable_3), .reset(RD_3));  // open: Qn
  Multiplexer #(.select(2)) multiplexer_11 (
    .in0(not_4_out), .in1(1'b0), .in2(1'b1), .in3(1'b0), .out(D1_3), .sel({Q1_3, Q0_3}));  // open: en
  Multiplexer #(.select(2)) multiplexer_12 (
    .in0(1'b0), .in1(not_4_out), .in2(not_5_out), .in3(1'b1), .out(D0_3), .sel({Q1_3, Q0_3}));  // open: en
  D_Flip_Flop d_ff_12 (.clk(button_3_out), .D(D0_3), .Q(Q0_3), .preset(SD_3), .en(Enable_3), .reset(RD_3));  // open: Qn
  Button button_4 (.out(button_4_out));
  not not_6 (not_6_out, Q3_4);
  D_Flip_Flop d_ff_13 (.clk(button_4_out), .D(D3_4), .Q(Q3_4), .preset(SD_4), .en(Enable_4), .reset(RD_4));  // open: Qn
  Multiplexer #(.select(2)) multiplexer_13 (
    .in0(1'b1), .in1(1'b0), .in2(1'b0), .in3(1'b0), .out(D3_4), .sel({Q1_4, Q0_4}));  // open: en
  Multiplexer #(.select(2)) multiplexer_14 (
    .in0(not_6_out), .in1(1'b0), .in2(1'b1), .in3(1'b0), .out(D2_4), .sel({Q1_4, Q0_4}));  // open: en
  D_Flip_Flop d_ff_14 (.clk(button_4_out), .D(D2_4), .Q(Q2_4), .preset(SD_4), .en(Enable_4), .reset(RD_4));  // open: Qn
  not not_7 (not_7_out, Q2_4);
  D_Flip_Flop d_ff_15 (.clk(button_4_out), .D(D1_4), .Q(Q1_4), .preset(SD_4), .en(Enable_4), .reset(RD_4));  // open: Qn
  Multiplexer #(.select(2)) multiplexer_15 (
    .in0(1'b0), .in1(not_6_out), .in2(not_7_out), .in3(1'b1), .out(D1_4), .sel({Q1_4, Q0_4}));  // open: en
  Multiplexer #(.select(2)) multiplexer_16 (
    .in0(not_7_out), .in1(1'b1), .in2(1'b0), .in3(1'b0), .out(D0_4), .sel({Q1_4, Q0_4}));  // open: en
  D_Flip_Flop d_ff_16 (.clk(button_4_out), .D(D0_4), .Q(Q0_4), .preset(SD_4), .en(Enable_4), .reset(RD_4));  // open: Qn

  // Notes on the sheet:
  //   B1
  //   Additya Akash Mishra
  //   BT20HCS081
  //   8505854809
  //   Decadee Up Counter
  //   Decade Down Counter
  //   Sequence Generator Clock Wise (Rotation of Bit)
  //   Sequence Generator Anti-Clock Wise
endmodule
