// Logisim project Hamming Code Transmitter and Reciever.circ as structural Verilog: 6 circuits, main circuit main
module main (
  input  D7,
  input  D6,
  input  D5,
  input  D3,
  output D7_2,
  output D6_2,
  output D5_2,
  output P4,
  output D3_2,
  output P2,
  output P1,
  output D7_3,
  output D6_3,
  output D5_3,
  output P4_2,
  output D3_3,
  output P2_2,
  output P1_2
);

  Hamming_Code_Transmitter_Even_Parity hamming_code_transmitter_even_parity_1 (
    .D7(D7), .D6(D6), .D5(D5), .D3(D3), .D6_2(D6_3), .D5_2(D5_3), .P4(P4_2), .D3_2(D3_3), .P2(P2_2),
    .P1(P1_2), .D7_2(D7_3));
  Hamming_Code_Transmitter_Odd_Parity hamming_code_transmitter_odd_parity_1 (
    .D3(D3), .D5(D5), .D6(D6), .D7(D7), .P1(P1), .P2(P2), .D3_2(D3_2), .P4(P4), .D5_2(D5_2), .D6_2(D6_2),
    .D7_2(D7_2));
endmodule

module Hamming_Code_Transmitter_Even_Parity (
  input  D7,
  input  D6,
  input  D5,
  input  D3,
  output D7_2,
  output D6_2,
  output D5_2,
  output P4,
  output D3_2,
  output P2,
  output P1
);

  wire xor_1_out, xor_3_out, xor_5_out;

  xor xor_1 (xor_1_out, D3, D5);
  xor xor_2 (P1, xor_1_out, D7);
  xor xor_3 (xor_3_out, D3, D6);
  xor xor_4 (P2, xor_3_out, D7);
  xor xor_5 (xor_5_out, D5, D6);
  xor xor_6 (P4, xor_5_out, D7);

  assign D3_2 = D3;
  assign D5_2 = D5;
  assign D6_2 = D6;
  assign D7_2 = D7;
endmodule

module Hamming_Code_Transmitter_Odd_Parity (
  input  D3,
  input  D5,
  input  D6,
  input  D7,
  output P1,
  output P2,
  output D3_2,
  output P4,
  output D5_2,
  output D6_2,
  output D7_2
);

  wire hamming_code_transmitter_even_parity_1_p1, hamming_code_transmitter_even_parity_1_p2,
       hamming_code_transmitter_even_parity_1_p4;

  Hamming_Code_Transmitter_Even_Parity hamming_code_transmitter_even_parity_1 (
    .D7(D7), .D6(D6), .D5(D5), .D3(D3), .D6_2(D6_2), .D5_2(D5_2),
    .P4(hamming_code_transmitter_even_parity_1_p4), .D3_2(D3_2),
    .P2(hamming_code_transmitter_even_parity_1_p2), .P1(hamming_code_transmitter_even_parity_1_p1),
    .D7_2(D7_2));
  not not_1 (P1, hamming_code_transmitter_even_parity_1_p1);
  not not_2 (P2, hamming_code_transmitter_even_parity_1_p2);
  not not_3 (P4, hamming_code_transmitter_even_parity_1_p4);
endmodule

module Hamming_Code_Detector_O (
  input  P1,
  input  P2,
  input  D3,
  input  P4,
  input  D5,
  input  D6,
  input  D7,
  output X,
  output Y,
  output Z
);

  ExactlyOne u_X (.out(X), .in0(P1), .in1(D3), .in2(D5), .in3(D7));
  ExactlyOne u_Y (.out(Y), .in0(P2), .in1(D3), .in2(D6), .in3(D7));
  ExactlyOne u_Z (.out(Z), .in0(P4), .in1(D5), .in2(D6), .in3(D7));
endmodule

module Haming_Code_Corrector (
  input  P1,
  input  P2,
  input  D3,
  input  P4,
  input  D5,
  input  D6,
  input  D7,
  input  Z,
  input  Y,
  input  X,
  output out_11
);

  wire multiplexer_1_out;

  Multiplexer #(.select(3)) multiplexer_1 (
    .in0(1'b1), .in1(P1), .in2(P2), .in3(D3), .in4(P4), .in5(D5), .in6(D6), .in7(D7),
    .out(multiplexer_1_out), .sel({Z, Y, X}), .en(1'b1));
  not not_1 (out_11, multiplexer_1_out);
endmodule

module Hamming_Code_Detector_E (
  input  P1,
  input  P2,
  input  D3,
  input  P4,
  input  D5,
  input  D6,
  input  D7,
  output X,
  output Y,
  output Z
);

  ExactlyOne u_X (.out(X), .in0(P1), .in1(D3), .in2(D5), .in3(D7));
  ExactlyOne u_Y (.out(Y), .in0(P2), .in1(D3), .in2(D6), .in3(D7));
  ExactlyOne u_Z (.out(Z), .in0(P4), .in1(D5), .in2(D6), .in3(D7));
endmodule
