// Logisim project Practical - 1 Half-Full Adder-Subtractor Flip-Flops.circ as structural Verilog: 1 circuit, main circuit main
module main (
  input  A,
  input  A_2,
  input  B,
  input  B_2,
  input  C,
  input  A1,
  input  A2,
  input  A3,
  input  A4,
  input  B1,
  input  B2,
  input  B3,
  input  B4,
  input  A_3,
  input  A_4,
  input  B_3,
  input  B_4,
  input  C_2,
  input  D,
  input  User,
  input  A_5,
  input  B_5,
  input  J,
  input  K,
  input  T,
  output Sum,
  output Sum_2,
  output D1,
  output D2,
  output D3,
  output D4,
  output Carry,
  output Carry_2,
  output Borrow,
  output Difference,
  output Difference_2,
  output Borrow_2,
  output Borrow_3,
  output Qm,
  output Qs,
  output Qm_prime,
  output Qs_prime,
  output Sum_Difference,
  output Qm_2,
  output Qs_2,
  output Carry_Borrow,
  output Qm_prime_2,
  output Qs_prime_2,
  output Qm_3,
  output Qs_3,
  output Qm_prime_3,
  output Qs_prime_3
);

  wire adder_1_cout, adder_1_out, adder_2_cout, adder_2_out, adder_3_cout, adder_3_out, adder_4_cout,
       adder_4_out, adder_5_cout, adder_6_cout, adder_7_cout, and_4_out, and_5_out, and_6_out, and_7_out,
       clock_1_out, clock_2_out, clock_3_out, nand_1_out, nand_2_out, nand_3_out, nand_4_out, nand_5_out,
       nand_6_out, nor_1_out, nor_2_out, nor_3_out, nor_4_out, nor_5_out, nor_6_out, not_1_out, not_2_out,
       not_3_out, not_4_out, not_5_out, not_6_out, not_7_out, not_8_out, not_9_out, xor_3_out, xor_5_out,
       xor_6_out, xor_9_out, xor_10_out, xor_11_out, xor_12_out;

  xor xor_1 (Sum, A_2, B_2);
  and and_1 (Carry, A_2, B_2);
  xor xor_2 (Difference_2, A_4, B_4);
  not not_1 (not_1_out, A_4);
  and and_2 (Borrow_3, not_1_out, B_4);
  xor xor_3 (xor_3_out, A_5, User);
  xor xor_4 (Sum_Difference, A_5, B_5);
  and and_3 (Carry_Borrow, xor_3_out, B_5);
  xor xor_5 (xor_5_out, A, B);
  xor xor_6 (xor_6_out, B_3, C_2);
  not not_2 (not_2_out, B_3);
  and and_4 (and_4_out, not_2_out, C_2);
  and and_5 (and_5_out, xor_5_out, C);
  and and_6 (and_6_out, A, B);
  xor xor_7 (Difference, A_3, xor_6_out);
  not not_3 (not_3_out, xor_6_out);
  xor xor_8 (Sum_2, xor_5_out, C);
  or or_1 (Carry_2, and_5_out, and_6_out);
  and and_7 (and_7_out, not_3_out, A_3);
  or or_2 (Borrow_2, and_7_out, and_4_out);
  Clock clock_1 (.out(clock_1_out));
  not not_4 (not_4_out, D);
  Clock clock_2 (.out(clock_2_out));
  Clock clock_3 (.out(clock_3_out));
  nand nand_1 (nand_1_out, Qs_prime, D, clock_1_out);
  nand nand_2 (nand_2_out, clock_1_out, not_4_out, Qs);
  nand nand_3 (nand_3_out, Qs_prime_2, J, clock_2_out);
  nand nand_4 (nand_4_out, clock_2_out, K, Qs_2);
  nand nand_5 (nand_5_out, Qs_prime_3, T, clock_3_out);
  nand nand_6 (nand_6_out, clock_3_out, T, Qs_3);
  nand nand_7 (Qm, nand_1_out, Qm_prime);
  nand nand_8 (Qm_prime, Qm, nand_2_out);
  nand nand_9 (Qm_2, nand_3_out, Qm_prime_2);
  nand nand_10 (Qm_prime_2, Qm_2, nand_4_out);
  nand nand_11 (Qm_3, nand_5_out, Qm_prime_3);
  nand nand_12 (Qm_prime_3, Qm_3, nand_6_out);
  Adder #(.width(1)) adder_1 (.a(A1), .b(not_5_out), .out(adder_1_out), .cin(1'b1), .cout(adder_1_cout));
  not not_5 (not_5_out, B1);
  Adder #(.width(1)) adder_2 (.a(A2), .b(not_6_out), .out(adder_2_out), .cin(adder_1_cout), .cout(adder_2_cout));
  not not_6 (not_6_out, B2);
  Adder #(.width(1)) adder_3 (.a(A3), .b(not_7_out), .out(adder_3_out), .cin(adder_2_cout), .cout(adder_3_cout));
  not not_7 (not_7_out, B3);
  Adder #(.width(1)) adder_4 (.a(A4), .b(not_8_out), .out(adder_4_out), .cin(adder_3_cout), .cout(adder_4_cout));
  not not_8 (not_8_out, B4);
  not not_9 (not_9_out, adder_4_cout);
  nor nor_1 (nor_1_out, Qm, clock_1_out);
  nor nor_2 (nor_2_out, clock_1_out, Qm_prime);
  nor nor_3 (nor_3_out, Qm_2, clock_2_out);
  nor nor_4 (nor_4_out, clock_2_out, Qm_prime_2);
  nor nor_5 (nor_5_out, Qm_3, clock_3_out);
  nor nor_6 (nor_6_out, clock_3_out, Qm_prime_3);
  nor nor_7 (Qs, Qs_prime, nor_1_out);
  nor nor_8 (Qs_prime, nor_2_out, Qs);
  nor nor_9 (Qs_2, Qs_prime_2, nor_3_out);
  nor nor_10 (Qs_prime_2, nor_4_out, Qs_2);
  nor nor_11 (Qs_3, Qs_prime_3, nor_5_out);
  nor nor_12 (Qs_prime_3, nor_6_out, Qs_3);
  xor xor_9 (xor_9_out, adder_1_out, not_9_out);
  xor xor_10 (xor_10_out, adder_2_out, not_9_out);
  xor xor_11 (xor_11_out, adder_3_out, not_9_out);
  xor xor_12 (xor_12_out, adder_4_out, not_9_out);
  Adder #(.width(1)) adder_5 (.a(1'b0), .b(xor_9_out), .out(D1), .cin(not_9_out), .cout(adder_5_cout));
  Adder #(.width(1)) adder_6 (.a(1'b0), .b(xor_10_out), .out(D2), .cin(adder_5_cout), .cout(adder_6_cout));
  Adder #(.width(1)) adder_7 (.a(1'b0), .b(xor_11_out), .out(D3), .cin(adder_6_cout), .cout(adder_7_cout));
  Adder #(.width(1)) adder_8 (.a(1'b0), .b(xor_12_out), .out(D4), .cin(adder_7_cout), .cout(Borrow));

  // Notes on the sheet:
  //   Half/Full Adder
  //   Half/Full Subtractor
  //   User Input
  //   Additya Akash Mishra
  //   B-1
  //   8505854809
  //   Week 1 Practical
  //   Subtraction using 2's Compliment
  //   D Master Slave Flip Flop
  //   JK Master Slave Flip Flop
  //   T Master Slave Flip Flop
endmodule
