// Logisim project Practical - 3 Shift Register.circ as structural Verilog: 1 circuit, main circuit main
module main (
  input  Din,
  input  Preset,
  input  Enable,
  input  Preset_2,
  input  Clear,
  input  Enable_2,
  input  Clear_2,
  input  Din_2,
  input  Shift_Load,
  input  Preset_3,
  input  Enable_3,
  input  Clear_3,
  input  DR,
  input  DL,
  input  Preset_4,
  input  Enable_4,
  input  Clear_4,
  input  D0,
  input  D1,
  input  D2,
  input  D3,
  input  Preset_5,
  input  Enable_5,
  input  Preset_6,
  input  Clear_5,
  input  Enable_6,
  input  Clear_6,
  input  Shift_Load_2,
  input  in_29,
  input  in_30,
  input  in_31,
  input  in_32,
  input  D0_2,
  input  D1_2,
  input  D2_2,
  input  D3_2,
  input  Load_Shift,
  output Output,
  output Q0,
  output Q1,
  output Q2,
  output Q3,
  output Q0_2,
  output Q1_2,
  output Q2_2,
  output Q3_2,
  output Q3_3,
  output Q3_4
);

  wire and_1_out, and_2_out, and_3_out, and_4_out, and_5_out, and_6_out, and_7_out, and_8_out, and_9_out,
       and_10_out, and_11_out, and_12_out, and_13_out, and_14_out, and_15_out, and_16_out, Clock_2_out,
       Clock_3_out, Clock_4_out, Clock_5_out, Clock_6_out, Clock_out, d_ff_1_q, d_ff_4_q, d_ff_5_q, d_ff_6_q,
       d_ff_11_q, d_ff_15_q, d_ff_17_q, d_ff_18_q, d_ff_19_q, d_ff_20_q, d_ff_21_q, d_ff_22_q, d_ff_23_q,
       multiplexer_1_out, multiplexer_2_out, multiplexer_3_out, not_1_out, not_2_out, or_1_out, or_2_out,
       or_3_out, or_4_out, or_5_out, or_6_out, or_7_out;

  Button Clock (.out(Clock_out));
  Button Clock_2 (.out(Clock_2_out));
  Button Clock_3 (.out(Clock_3_out));
  Button Clock_4 (.out(Clock_4_out));
  and and_1 (and_1_out, D0_2, not_1_out);
  not not_1 (not_1_out, Shift_Load_2);
  D_Flip_Flop d_ff_1 (.clk(Clock_out), .D(Din), .Q(d_ff_1_q), .preset(Preset), .en(Enable), .reset(Clear));  // open: Qn
  D_Flip_Flop d_ff_2 (
    .clk(Clock_2_out), .D(Din_2), .Q(Q0), .preset(Preset_3), .en(Enable_3), .reset(Clear_3));  // open: Qn
  D_Flip_Flop d_ff_3 (
    .clk(Clock_3_out), .D(D0), .Q(Q0_2), .preset(Preset_4), .en(Enable_4), .reset(Clear_4));  // open: Qn
  D_Flip_Flop d_ff_4 (
    .clk(Clock_4_out), .D(and_1_out), .Q(d_ff_4_q), .preset(Preset_6), .en(Enable_6), .reset(Clear_6));  // open: Qn
  or or_1 (or_1_out, and_2_out, and_3_out);
  and and_2 (and_2_out, d_ff_4_q, Shift_Load_2);
  and and_3 (and_3_out, not_1_out, D1_2);
  D_Flip_Flop d_ff_5 (
    .clk(Clock_out), .D(d_ff_6_q), .Q(d_ff_5_q), .preset(Preset), .en(Enable), .reset(Clear));  // open: Qn
  D_Flip_Flop d_ff_6 (
    .clk(Clock_out), .D(d_ff_1_q), .Q(d_ff_6_q), .preset(Preset), .en(Enable), .reset(Clear));  // open: Qn
  D_Flip_Flop d_ff_7 (
    .clk(Clock_2_out), .D(Q0), .Q(Q1), .preset(Preset_3), .en(Enable_3), .reset(Clear_3));  // open: Qn
  D_Flip_Flop d_ff_8 (
    .clk(Clock_2_out), .D(Q1), .Q(Q2), .preset(Preset_3), .en(Enable_3), .reset(Clear_3));  // open: Qn
  D_Flip_Flop d_ff_9 (
    .clk(Clock_3_out), .D(D1), .Q(Q1_2), .preset(Preset_4), .en(Enable_4), .reset(Clear_4));  // open: Qn
  D_Flip_Flop d_ff_10 (
    .clk(Clock_3_out), .D(D2), .Q(Q2_2), .preset(Preset_4), .en(Enable_4), .reset(Clear_4));  // open: Qn
  D_Flip_Flop d_ff_11 (
    .clk(Clock_4_out), .D(or_1_out), .Q(d_ff_11_q), .preset(Preset_6), .en(Enable_6), .reset(Clear_6));  // open: Qn
  or or_2 (or_2_out, and_5_out, and_4_out);
  and and_4 (and_4_out, not_1_out, D2_2);
  and and_5 (and_5_out, d_ff_11_q, Shift_Load_2);
  D_Flip_Flop d_ff_12 (
    .clk(Clock_out), .D(d_ff_5_q), .Q(Output), .preset(Preset), .en(Enable), .reset(Clear));  // open: Qn
  D_Flip_Flop d_ff_13 (
    .clk(Clock_2_out), .D(Q2), .Q(Q3), .preset(Preset_3), .en(Enable_3), .reset(Clear_3));  // open: Qn
  D_Flip_Flop d_ff_14 (
    .clk(Clock_3_out), .D(D3), .Q(Q3_2), .preset(Preset_4), .en(Enable_4), .reset(Clear_4));  // open: Qn
  D_Flip_Flop d_ff_15 (
    .clk(Clock_4_out), .D(or_2_out), .Q(d_ff_15_q), .preset(Preset_6), .en(Enable_6), .reset(Clear_6));  // open: Qn
  or or_3 (or_3_out, and_6_out, and_7_out);
  and and_6 (and_6_out, d_ff_15_q, Shift_Load_2);
  and and_7 (and_7_out, not_1_out, D3_2);
  D_Flip_Flop d_ff_16 (
    .clk(Clock_4_out), .D(or_3_out), .Q(Q3_4), .preset(Preset_6), .en(Enable_6), .reset(Clear_6));  // open: Qn
  Button Clock_5 (.out(Clock_5_out));
  not not_2 (not_2_out, Shift_Load);
  or or_4 (or_4_out, and_8_out, and_9_out);
  and and_8 (and_8_out, DR, Shift_Load);
  and and_9 (and_9_out, not_2_out, d_ff_19_q);
  LED led_1 (.in(d_ff_17_q));
  D_Flip_Flop d_ff_17 (
    .clk(Clock_5_out), .D(or_4_out), .Q(d_ff_17_q), .preset(Preset_2), .en(Enable_2), .reset(Clear_2));  // open: Qn
  or or_5 (or_5_out, and_11_out, and_10_out);
  and and_10 (and_10_out, not_2_out, d_ff_18_q);
  and and_11 (and_11_out, d_ff_17_q, Shift_Load);
  LED led_2 (.in(d_ff_19_q));
  D_Flip_Flop d_ff_18 (
    .clk(Clock_5_out), .D(or_6_out), .Q(d_ff_18_q), .preset(Preset_2), .en(Enable_2), .reset(Clear_2));  // open: Qn
  D_Flip_Flop d_ff_19 (
    .clk(Clock_5_out), .D(or_5_out), .Q(d_ff_19_q), .preset(Preset_2), .en(Enable_2), .reset(Clear_2));  // open: Qn
  or or_6 (or_6_out, and_12_out, and_13_out);
  and and_12 (and_12_out, d_ff_19_q, Shift_Load);
  and and_13 (and_13_out, not_2_out, d_ff_20_q);
  LED led_3 (.in(d_ff_20_q));
  LED led_4 (.in(d_ff_18_q));
  D_Flip_Flop d_ff_20 (
    .clk(Clock_5_out), .D(or_7_out), .Q(d_ff_20_q), .preset(Preset_2), .en(Enable_2), .reset(Clear_2));  // open: Qn
  or or_7 (or_7_out, and_14_out, and_15_out);
  and and_14 (and_14_out, d_ff_18_q, Shift_Load);
  and and_15 (and_15_out, not_2_out, DL);
  Button Clock_6 (.out(Clock_6_out));
  D_Flip_Flop d_ff_21 (
    .clk(Clock_6_out), .D(and_16_out), .Q(d_ff_21_q), .preset(Preset_5), .en(Enable_5), .reset(Clear_5));  // open: Qn
  and and_16 (and_16_out, in_29, Load_Shift);
  D_Flip_Flop d_ff_22 (
    .clk(Clock_6_out), .D(multiplexer_1_out), .Q(d_ff_22_q), .preset(Preset_5), .en(Enable_5), .reset(Clear_5));  // open: Qn
  Multiplexer multiplexer_1 (.in0(d_ff_21_q), .in1(in_30), .out(multiplexer_1_out), .sel(Load_Shift));  // open: en
  D_Flip_Flop d_ff_23 (
    .clk(Clock_6_out), .D(multiplexer_2_out), .Q(d_ff_23_q), .preset(Preset_5), .en(Enable_5), .reset(Clear_5));  // open: Qn
  Multiplexer multiplexer_2 (.in0(d_ff_22_q), .in1(in_31), .out(multiplexer_2_out), .sel(Load_Shift));  // open: en
  D_Flip_Flop d_ff_24 (
    .clk(Clock_6_out), .D(multiplexer_3_out), .Q(Q3_3), .preset(Preset_5), .en(Enable_5), .reset(Clear_5));  // open: Qn
  Multiplexer multiplexer_3 (.in0(d_ff_23_q), .in1(in_32), .out(multiplexer_3_out), .sel(Load_Shift));  // open: en

  // Notes on the sheet:
  //   SISO
  //   SIPO
  //   PIPO
  //   PISO
  //   Additya Akash Mishra
  //   B - 1
  //   BT20HCS081
  //   8505854809
  //   Practical - 3
  //   Bi-Directionial Shift Register
  //   PISO
endmodule
