// Logisim project Practical - 7 (4x4 RAM Cell).circ as structural Verilog: 2 circuits, main circuit RAM Cell
module RAM_Cell (
  input  Select,
  input  Input,
  input  clk,
  input  Read_Write,
  output Memory_Data,
  output Output
);

  wire and_1_out, and_2_out, not_1_out, not_2_out;

  not not_1 (not_1_out, Input);
  and and_1 (and_1_out, Select, Input, not_2_out);
  and and_2 (and_2_out, Select, not_1_out, not_2_out);
  not not_2 (not_2_out, Read_Write);
  S_R_Flip_Flop s_r_ff_1 (.S(and_1_out), .clk(clk), .R(and_2_out), .Q(Memory_Data));  // open: Qn, preset, reset, en
  and and_3 (Output, Select, Memory_Data, Read_Write);

  // Notes on the sheet:
  //   Additya Akash Mishra
  //   BT20HCS081
  //   8505854809
  //   B-1
endmodule

module Main (
  input  I1,
  input  I2,
  input  I3,
  input  I4,
  input  in_5,
  input  I5,
  input  in_7,
  input  I6,
  input  I7,
  input  I8,
  input  I9,
  input  I10,
  input  I11,
  input  I12,
  input  I13,
  input  I14,
  input  I15,
  input  I16,
  input  Write_Read,
  output MD1,
  output MD2,
  output MD3,
  output MD4,
  output MD5,
  output MD6,
  output MD7,
  output MD8,
  output MD9,
  output MD10,
  output MD11,
  output MD12,
  output MD13,
  output MD14,
  output MD15,
  output MD16,
  output O1,
  output O2,
  output O3,
  output O4,
  output O5,
  output O6,
  output O7,
  output O8,
  output O9,
  output O10,
  output O11,
  output O12,
  output O13,
  output O14,
  output O15,
  output O16
);

  wire clk_out, decoder_1_out0, decoder_1_out1, decoder_1_out2, decoder_1_out3;

  Decoder #(.select(2)) decoder_1 (
    .out0(decoder_1_out0), .out1(decoder_1_out1), .out2(decoder_1_out2), .out3(decoder_1_out3),
    .sel({in_7, in_5}));  // open: en
  Clock clk (.out(clk_out));
  RAM_Cell ram_cell_1 (
    .Input(I1), .clk(clk_out), .Memory_Data(MD1), .Output(O1), .Select(decoder_1_out0),
    .Read_Write(Write_Read));
  RAM_Cell ram_cell_2 (
    .Input(I2), .clk(clk_out), .Memory_Data(MD2), .Output(O2), .Select(decoder_1_out0),
    .Read_Write(Write_Read));
  RAM_Cell ram_cell_3 (
    .Input(I5), .clk(clk_out), .Memory_Data(MD5), .Output(O5), .Select(decoder_1_out1),
    .Read_Write(Write_Read));
  RAM_Cell ram_cell_4 (
    .Input(I6), .clk(clk_out), .Memory_Data(MD6), .Output(O6), .Select(decoder_1_out1),
    .Read_Write(Write_Read));
  RAM_Cell ram_cell_5 (
    .Input(I9), .clk(clk_out), .Memory_Data(MD9), .Output(O9), .Select(decoder_1_out2),
    .Read_Write(Write_Read));
  RAM_Cell ram_cell_6 (
    .Input(I10), .clk(clk_out), .Memory_Data(MD10), .Output(O10), .Select(decoder_1_out2),
    .Read_Write(Write_Read));
  RAM_Cell ram_cell_7 (
    .Input(I13), .clk(clk_out), .Memory_Data(MD13), .Output(O13), .Select(decoder_1_out3),
    .Read_Write(Write_Read));
  RAM_Cell ram_cell_8 (
    .Input(I14), .clk(clk_out), .Memory_Data(MD14), .Output(O14), .Select(decoder_1_out3),
    .Read_Write(Write_Read));
  RAM_Cell ram_cell_9 (
    .Input(I3), .clk(clk_out), .Memory_Data(MD3), .Output(O3), .Select(decoder_1_out0),
    .Read_Write(Write_Read));
  RAM_Cell ram_cell_10 (
    .Input(I4), .clk(clk_out), .Memory_Data(MD4), .Output(O4), .Select(decoder_1_out0),
    .Read_Write(Write_Read));
  RAM_Cell ram_cell_11 (
    .Input(I7), .clk(clk_out), .Memory_Data(MD7), .Output(O7), .Select(decoder_1_out1),
    .Read_Write(Write_Read));
  RAM_Cell ram_cell_12 (
    .Input(I8), .clk(clk_out), .Memory_Data(MD8), .Output(O8), .Select(decoder_1_out1),
    .Read_Write(Write_Read));
  RAM_Cell ram_cell_13 (
    .Input(I11), .clk(clk_out), .Memory_Data(MD11), .Output(O11), .Select(decoder_1_out2),
    .Read_Write(Write_Read));
  RAM_Cell ram_cell_14 (
    .Input(I12), .clk(clk_out), .Memory_Data(MD12), .Output(O12), .Select(decoder_1_out2),
    .Read_Write(Write_Read));
  RAM_Cell ram_cell_15 (
    .Input(I15), .clk(clk_out), .Memory_Data(MD15), .Output(O15), .Select(decoder_1_out3),
    .Read_Write(Write_Read));
  RAM_Cell ram_cell_16 (
    .Input(I16), .clk(clk_out), .Memory_Data(MD16), .Output(O16), .Select(decoder_1_out3),
    .Read_Write(Write_Read));

  // Notes on the sheet:
  //   Input Data
  //   Memory Data
  //   Additya Akash Mishra
  //   BT20HCS081
  //   8505854809
  //   B-1
  //   Output Data
endmodule
