// Logisim project Practice.circ as structural Verilog: 1 circuit, main circuit main
module main (
  input  A1,
  input  A2,
  input  A3,
  input  A4,
  input  B1,
  input  B2,
  input  B3,
  input  B4,
  input  A1_2,
  input  A2_2,
  input  A3_2,
  input  A4_2,
  input  B1_2,
  input  B2_2,
  input  B3_2,
  input  B4_2,
  output C1,
  output C2,
  output C3,
  output C4,
  output C1_2,
  output C2_2,
  output C3_2,
  output C4_2
);

  wire adder_1_cout, adder_1_out, adder_2_cout, adder_2_out, adder_3_cout, adder_3_out, adder_4_cout,
       adder_4_out, adder_5_cout, adder_5_out, adder_6_cout, adder_6_out, adder_7_cout, adder_7_out,
       adder_8_cout, adder_8_out, adder_9_cout, adder_10_cout, adder_11_cout, adder_12_cout, adder_13_cout,
       adder_14_cout, adder_15_cout, adder_16_cout, not_1_out, not_2_out, not_3_out, not_4_out, not_5_out,
       not_6_out, not_7_out, not_8_out, not_9_out, not_10_out, xor_1_out, xor_2_out, xor_3_out, xor_4_out,
       xor_5_out, xor_6_out, xor_7_out, xor_8_out;

  Adder #(.width(1)) adder_1 (.a(A1), .b(not_1_out), .out(adder_1_out), .cout(adder_1_cout));  // open: cin
  not not_1 (not_1_out, B1);
  Adder #(.width(1)) adder_2 (.a(A2), .b(not_2_out), .out(adder_2_out), .cin(adder_1_cout), .cout(adder_2_cout));
  not not_2 (not_2_out, B2);
  Adder #(.width(1)) adder_3 (.a(A3), .b(not_3_out), .out(adder_3_out), .cin(adder_2_cout), .cout(adder_3_cout));
  not not_3 (not_3_out, B3);
  Adder #(.width(1)) adder_4 (.a(A4), .b(not_4_out), .out(adder_4_out), .cin(adder_3_cout), .cout(adder_4_cout));
  not not_4 (not_4_out, B4);
  not not_5 (not_5_out, adder_4_cout);
  Adder #(.width(1)) adder_5 (.a(A1_2), .b(not_6_out), .out(adder_5_out), .cin(1'b1), .cout(adder_5_cout));
  not not_6 (not_6_out, B1_2);
  Adder #(.width(1)) adder_6 (.a(A2_2), .b(not_7_out), .out(adder_6_out), .cin(adder_5_cout), .cout(adder_6_cout));
  not not_7 (not_7_out, B2_2);
  Adder #(.width(1)) adder_7 (.a(A3_2), .b(not_8_out), .out(adder_7_out), .cin(adder_6_cout), .cout(adder_7_cout));
  not not_8 (not_8_out, B3_2);
  Adder #(.width(1)) adder_8 (.a(A4_2), .b(not_9_out), .out(adder_8_out), .cin(adder_7_cout), .cout(adder_8_cout));
  not not_9 (not_9_out, B4_2);
  not not_10 (not_10_out, adder_8_cout);
  xor xor_1 (xor_1_out, adder_1_out, not_5_out);
  xor xor_2 (xor_2_out, adder_2_out, not_5_out);
  xor xor_3 (xor_3_out, adder_3_out, not_5_out);
  xor xor_4 (xor_4_out, adder_4_out, not_5_out);
  xor xor_5 (xor_5_out, adder_5_out, not_10_out);
  xor xor_6 (xor_6_out, adder_6_out, not_10_out);
  xor xor_7 (xor_7_out, adder_7_out, not_10_out);
  xor xor_8 (xor_8_out, adder_8_out, not_10_out);
  Adder #(.width(1)) adder_9 (.a(not_5_out), .b(xor_1_out), .out(C1), .cout(adder_9_cout));  // open: cin
  Adder #(.width(1)) adder_10 (.a(1'b0), .b(xor_2_out), .out(C2), .cin(adder_9_cout), .cout(adder_10_cout));
  Adder #(.width(1)) adder_11 (.a(1'b0), .b(xor_3_out), .out(C3), .cin(adder_10_cout), .cout(adder_11_cout));
  Adder #(.width(1)) adder_12 (.a(1'b0), .b(xor_4_out), .out(C4), .cin(adder_11_cout), .cout(adder_12_cout));
  Adder #(.width(1)) adder_13 (.a(not_10_out), .b(xor_5_out), .out(C1_2), .cin(not_10_out), .cout(adder_13_cout));
  Adder #(.width(1)) adder_14 (.a(1'b0), .b(xor_6_out), .out(C2_2), .cin(adder_13_cout), .cout(adder_14_cout));
  Adder #(.width(1)) adder_15 (.a(1'b0), .b(xor_7_out), .out(C3_2), .cin(adder_14_cout), .cout(adder_15_cout));
  Adder #(.width(1)) adder_16 (.a(1'b0), .b(xor_8_out), .out(C4_2), .cin(adder_15_cout), .cout(adder_16_cout));
endmodule
