// Logisim project RING_JHONSON_MLS.circ as structural Verilog: 1 circuit, main circuit main
module main (
);

  wire button_1_out, button_2_out, button_3_out, button_4_out, button_5_out, button_6_out, button_7_out,
       button_8_out, d_ff_1_q, d_ff_2_q, d_ff_3_q, d_ff_4_q, d_ff_5_q, d_ff_6_q, d_ff_7_q, d_ff_8_q,
       d_ff_9_q, d_ff_10_q, d_ff_11_q, d_ff_12_q, d_ff_13_q, d_ff_14_q, d_ff_15_q, d_ff_16_q, d_ff_17_q,
       d_ff_18_q, d_ff_19_q, d_ff_20_q, d_ff_21_q, d_ff_22_q, d_ff_23_q, d_ff_24_q, d_ff_25_q, d_ff_26_q,
       d_ff_27_q, d_ff_28_q, d_ff_29_q, d_ff_30_q, d_ff_31_q, d_ff_32_q, d_ff_33_q, d_ff_34_q, d_ff_35_q,
       d_ff_36_q, d_ff_37_q, d_ff_38_q, d_ff_39_q, d_ff_39_qn, not_1_out, not_2_out, not_3_out, xor_1_out,
       xor_2_out;

  Button button_1 (.out(button_1_out));
  Button button_2 (.out(button_2_out));
  Button button_3 (.out(button_3_out));
  Button button_4 (.out(button_4_out));
  Button button_5 (.out(button_5_out));
  Button button_6 (.out(button_6_out));
  D_Flip_Flop d_ff_1 (.clk(button_1_out), .D(d_ff_19_q), .Q(d_ff_1_q));  // open: Qn, preset, en, reset
  D_Flip_Flop d_ff_2 (.clk(button_2_out), .D(not_1_out), .Q(d_ff_2_q));  // open: Qn, preset, en, reset
  D_Flip_Flop d_ff_3 (.clk(button_3_out), .D(d_ff_25_q), .Q(d_ff_3_q));  // open: Qn, preset, en, reset
  D_Flip_Flop d_ff_4 (.clk(button_4_out), .D(not_2_out), .Q(d_ff_4_q));  // open: Qn, preset, en, reset
  D_Flip_Flop d_ff_5 (.clk(button_5_out), .D(d_ff_27_q), .Q(d_ff_5_q));  // open: Qn, preset, en, reset
  D_Flip_Flop d_ff_6 (.clk(button_6_out), .D(not_3_out), .Q(d_ff_6_q));  // open: Qn, preset, en, reset
  LED led_1 (.in(d_ff_1_q));
  D_Flip_Flop d_ff_7 (.clk(button_1_out), .D(d_ff_1_q), .Q(d_ff_7_q));  // open: Qn, preset, en, reset
  LED led_2 (.in(d_ff_2_q));
  D_Flip_Flop d_ff_8 (.clk(button_2_out), .D(d_ff_2_q), .Q(d_ff_8_q));  // open: Qn, preset, en, reset
  LED led_3 (.in(d_ff_3_q));
  LED led_4 (.in(d_ff_4_q));
  LED led_5 (.in(d_ff_5_q));
  LED led_6 (.in(d_ff_6_q));
  LED led_7 (.in(d_ff_7_q));
  LED led_8 (.in(d_ff_8_q));
  LED led_9 (.in(d_ff_9_q));
  D_Flip_Flop d_ff_9 (.clk(button_3_out), .D(d_ff_3_q), .Q(d_ff_9_q));  // open: Qn, preset, en, reset
  LED led_10 (.in(d_ff_10_q));
  D_Flip_Flop d_ff_10 (.clk(button_4_out), .D(d_ff_4_q), .Q(d_ff_10_q));  // open: Qn, preset, en, reset
  LED led_11 (.in(d_ff_11_q));
  D_Flip_Flop d_ff_11 (.clk(button_5_out), .D(d_ff_5_q), .Q(d_ff_11_q));  // open: Qn, preset, en, reset
  D_Flip_Flop d_ff_12 (.clk(button_6_out), .D(d_ff_6_q), .Q(d_ff_12_q));  // open: Qn, preset, en, reset
  LED led_12 (.in(d_ff_13_q));
  D_Flip_Flop d_ff_13 (.clk(button_1_out), .D(d_ff_7_q), .Q(d_ff_13_q));  // open: Qn, preset, en, reset
  LED led_13 (.in(d_ff_14_q));
  D_Flip_Flop d_ff_14 (.clk(button_2_out), .D(d_ff_8_q), .Q(d_ff_14_q));  // open: Qn, preset, en, reset
  D_Flip_Flop d_ff_15 (.clk(button_3_out), .D(d_ff_9_q), .Q(d_ff_15_q));  // open: Qn, preset, en, reset
  D_Flip_Flop d_ff_16 (.clk(button_4_out), .D(d_ff_10_q), .Q(d_ff_16_q));  // open: Qn, preset, en, reset
  D_Flip_Flop d_ff_17 (.clk(button_5_out), .D(d_ff_11_q), .Q(d_ff_17_q));  // open: Qn, preset, en, reset
  LED led_14 (.in(d_ff_12_q));
  D_Flip_Flop d_ff_18 (.clk(button_6_out), .D(d_ff_12_q), .Q(d_ff_18_q));  // open: Qn, preset, en, reset
  LED led_15 (.in(d_ff_19_q));
  D_Flip_Flop d_ff_19 (.clk(button_1_out), .D(d_ff_13_q), .Q(d_ff_19_q));  // open: Qn, preset, en, reset
  not not_1 (not_1_out, d_ff_20_q);
  D_Flip_Flop d_ff_20 (.clk(button_2_out), .D(d_ff_14_q), .Q(d_ff_20_q));  // open: Qn, preset, en, reset
  LED led_16 (.in(d_ff_15_q));
  LED led_17 (.in(d_ff_16_q));
  LED led_18 (.in(d_ff_17_q));
  LED led_19 (.in(d_ff_18_q));
  LED led_20 (.in(d_ff_20_q));
  LED led_21 (.in(d_ff_21_q));
  D_Flip_Flop d_ff_21 (.clk(button_3_out), .D(d_ff_15_q), .Q(d_ff_21_q));  // open: Qn, preset, en, reset
  LED led_22 (.in(d_ff_22_q));
  not not_2 (not_2_out, d_ff_26_q);
  D_Flip_Flop d_ff_22 (.clk(button_4_out), .D(d_ff_16_q), .Q(d_ff_22_q));  // open: Qn, preset, en, reset
  LED led_23 (.in(d_ff_23_q));
  D_Flip_Flop d_ff_23 (.clk(button_5_out), .D(d_ff_17_q), .Q(d_ff_23_q));  // open: Qn, preset, en, reset
  LED led_24 (.in(d_ff_24_q));
  not not_3 (not_3_out, d_ff_29_q);
  D_Flip_Flop d_ff_24 (.clk(button_6_out), .D(d_ff_18_q), .Q(d_ff_24_q));  // open: Qn, preset, en, reset
  LED led_25 (.in(d_ff_25_q));
  D_Flip_Flop d_ff_25 (.clk(button_3_out), .D(d_ff_21_q), .Q(d_ff_25_q));  // open: Qn, preset, en, reset
  LED led_26 (.in(d_ff_26_q));
  D_Flip_Flop d_ff_26 (.clk(button_4_out), .D(d_ff_22_q), .Q(d_ff_26_q));  // open: Qn, preset, en, reset
  LED led_27 (.in(d_ff_27_q));
  LED led_28 (.in(d_ff_28_q));
  D_Flip_Flop d_ff_27 (.clk(button_5_out), .D(d_ff_28_q), .Q(d_ff_27_q));  // open: Qn, preset, en, reset
  D_Flip_Flop d_ff_28 (.clk(button_5_out), .D(d_ff_23_q), .Q(d_ff_28_q));  // open: Qn, preset, en, reset
  LED led_29 (.in(d_ff_29_q));
  LED led_30 (.in(d_ff_30_q));
  D_Flip_Flop d_ff_29 (.clk(button_6_out), .D(d_ff_30_q), .Q(d_ff_29_q));  // open: Qn, preset, en, reset
  D_Flip_Flop d_ff_30 (.clk(button_6_out), .D(d_ff_24_q), .Q(d_ff_30_q));  // open: Qn, preset, en, reset
  Button button_7 (.out(button_7_out));
  Button button_8 (.out(button_8_out));
  D_Flip_Flop d_ff_31 (.clk(button_8_out), .D(xor_2_out), .Q(d_ff_31_q));  // open: Qn, preset, en, reset
  D_Flip_Flop d_ff_32 (.clk(button_7_out), .D(xor_1_out), .Q(d_ff_32_q));  // open: Qn, preset, en, reset
  D_Flip_Flop d_ff_33 (.clk(button_8_out), .D(d_ff_31_q), .Q(d_ff_33_q));  // open: Qn, preset, en, reset
  LED led_31 (.in(d_ff_38_q));
  D_Flip_Flop d_ff_34 (.clk(button_7_out), .D(d_ff_32_q), .Q(d_ff_34_q));  // open: Qn, preset, en, reset
  LED led_32 (.in(d_ff_39_q));
  LED led_33 (.in(d_ff_37_q));
  D_Flip_Flop d_ff_35 (.clk(button_8_out), .D(d_ff_33_q), .Q(d_ff_35_q));  // open: Qn, preset, en, reset
  LED led_34 (.in(d_ff_34_q));
  LED led_35 (.in(d_ff_36_q));
  D_Flip_Flop d_ff_36 (.clk(button_7_out), .D(d_ff_34_q), .Q(d_ff_36_q));  // open: Qn, preset, en, reset
  LED led_36 (.in(d_ff_33_q));
  LED led_37 (.in(d_ff_35_q));
  LED led_38 (.in(d_ff_32_q));
  LED led_39 (.in(d_ff_31_q));
  D_Flip_Flop d_ff_37 (.clk(button_8_out), .D(d_ff_35_q), .Q(d_ff_37_q));  // open: Qn, preset, en, reset
  D_Flip_Flop d_ff_38 (.clk(button_7_out), .D(d_ff_36_q), .Q(d_ff_38_q));  // open: Qn, preset, en, reset
  D_Flip_Flop d_ff_39 (.clk(button_8_out), .D(d_ff_37_q), .Q(d_ff_39_q), .Qn(d_ff_39_qn));  // open: preset, en, reset
  xor xor_1 (xor_1_out, d_ff_38_q, d_ff_36_q);
  xor xor_2 (xor_2_out, d_ff_39_qn, d_ff_35_q);

  // Notes on the sheet:
  //   Q0
  //   Q0
  //   Q0
  //   Q0
  //   Q0
  //   Q0
  //   Q1
  //   Q1
  //   Q1
  //   Q1
  //   Q1
  //   Q1
  //   Q2
  //   Q2
  //   Q2
  //   Q2
  //   Q2
  //   Q2
  //   Q3
  //   Q3
  //   Q3
  //   Q3
  //   Q3
  //   Q4
  //   Q3
  //   Q4
  //   Q4
  //   Q4
  //   Q5
  //   Q5
  //   Additya Akash Mishra
  //   BT20HCS081
  //   B-1
  //   Q0
  //   Q1
  //   Q0
  //   Q1
  //   Q2
  //   Q3
  //   Q2
  //   Q3
  //   8505854809
  //   Q4
endmodule
