// Logisim project Sequence Detector.circ as structural Verilog: 1 circuit, main circuit main
module main (
  input  in_1,
  input  in_2,
  input  in_3,
  input  in_4,
  input  in_5,
  input  in_6,
  output out_7,
  output out_8,
  output out_9
);

  wire and_1_out, button_1_out, d_ff_1_q, d_ff_2_q, d_ff_3_q, decoder_1_out1, decoder_1_out2, decoder_1_out3,
       decoder_1_out5, decoder_1_out6, multiplexer_1_out, multiplexer_2_out, multiplexer_3_out, or_1_out,
       or_2_out;
  wire [0:0] d_ff_4_q;

  Button button_1 (.out(button_1_out));
  and and_1 (and_1_out, in_2, in_6);
  D_Flip_Flop d_ff_1 (.clk(button_1_out), .D(and_1_out), .Q(d_ff_1_q), .en(in_1));  // open: Qn, preset, reset
  D_Flip_Flop d_ff_2 (.clk(button_1_out), .D(multiplexer_1_out), .Q(d_ff_2_q), .en(in_1));  // open: Qn, preset, reset
  Multiplexer multiplexer_1 (.in0(d_ff_1_q), .in1(in_5), .out(multiplexer_1_out), .sel(in_2), .en(in_1));
  Multiplexer multiplexer_2 (.in0(d_ff_2_q), .in1(in_4), .out(multiplexer_2_out), .sel(in_2), .en(in_1));
  D_Flip_Flop d_ff_3 (.clk(button_1_out), .D(multiplexer_2_out), .Q(d_ff_3_q), .en(in_1));  // open: Qn, preset, reset
  Multiplexer multiplexer_3 (.in0(d_ff_3_q), .in1(in_3), .out(multiplexer_3_out), .sel(in_2), .en(in_1));
  D_Flip_Flop d_ff_4 (
    .clk(button_1_out), .D(multiplexer_3_out), .Q(d_ff_4_q[0]), .en(in_1));  // open: Qn, preset, reset
  Decoder #(.select(3)) decoder_1 (
    .out1(decoder_1_out1), .out2(decoder_1_out2), .out3(decoder_1_out3), .out5(decoder_1_out5),
    .out6(decoder_1_out6), .out7(out_7), .sel({out_8, out_9, d_ff_4_q[0]}), .en(in_1));  // open: out0, out4
  or or_1 (or_1_out, decoder_1_out2, decoder_1_out5, decoder_1_out6);
  or or_2 (or_2_out, decoder_1_out1, decoder_1_out3, decoder_1_out5, out_7);
  D_Flip_Flop d_ff_5 (.clk(button_1_out), .D(or_1_out), .Q(out_8), .en(in_1));  // open: Qn, preset, reset
  D_Flip_Flop d_ff_6 (.clk(button_1_out), .D(or_2_out), .Q(out_9), .en(in_1));  // open: Qn, preset, reset
endmodule
