// Logisim project Serial-Parallel Multiplier.circ as structural Verilog: 1 circuit, main circuit main
module main (
  input  in_1,
  input  in_2,
  input  in_3,
  input  in_4,
  input  in_5,
  input  in_6,
  input  in_7,
  input  in_8,
  input  in_9,
  input  D3,
  input  D2,
  input  D1,
  input  D0,
  output out_14,
  output out_15,
  output out_16,
  output out_17,
  output out_18,
  output out_19,
  output out_20,
  output out_21,
  output out_22,
  output out_23
);

  wire adder_1_cout, adder_1_out, adder_2_cout, adder_2_out, adder_3_cout, adder_3_out, adder_4_cout,
       adder_4_out, and_1_out, and_2_out, and_3_out, and_4_out, button_1_out, not_1_out, not_2_out;

  Button button_1 (.out(button_1_out));
  and and_1 (and_1_out, D3, out_23);
  and and_2 (and_2_out, D2, out_23);
  and and_3 (and_3_out, D1, out_23);
  and and_4 (and_4_out, D0, out_23);
  not not_1 (not_1_out, in_5);
  Shift_Register #(.length(4)) SR1 (
    .shift(not_1_out), .in(in_7), .clk(button_1_out), .out(out_14), .load(in_5), .clr(in_9),
    .d0(adder_4_out), .q0(out_16), .d1(adder_3_out), .q1(out_17), .d2(adder_2_out), .q2(out_18),
    .d3(adder_4_cout), .q3(out_19));
  Adder #(.width(1)) adder_1 (.a(and_1_out), .b(out_19), .out(adder_1_out), .cin(1'b0), .cout(adder_1_cout));
  Adder #(.width(1)) adder_2 (.a(and_2_out), .b(out_18), .out(adder_2_out), .cin(adder_1_cout), .cout(adder_2_cout));
  Adder #(.width(1)) adder_3 (.a(and_3_out), .b(out_17), .out(adder_3_out), .cin(adder_2_cout), .cout(adder_3_cout));
  Adder #(.width(1)) adder_4 (.a(and_4_out), .b(out_16), .out(adder_4_out), .cin(adder_3_cout), .cout(adder_4_cout));
  not not_2 (not_2_out, in_6);
  Shift_Register #(.length(4)) SR0 (
    .shift(not_2_out), .in(in_8), .clk(button_1_out), .out(out_15), .load(in_6), .clr(adder_1_out),
    .d0(in_1), .q0(out_20), .d1(in_2), .q1(out_21), .d2(in_3), .q2(out_22), .d3(in_4), .q3(out_23));

  // Notes on the sheet:
  //   Additya Akash Mishra 
  //   BT20HCS081
  //   B2
  //   8505854809
endmodule
