// Logisim project Universal Register.circ as structural Verilog: 1 circuit, main circuit main
module main (
  input  S2,
  input  Data_In_for_Serial_In,
  input  S1,
  input  S0,
  input  in_5,
  input  in_6,
  input  in_7,
  input  in_8,
  input  Enable,
  output out_10,
  output out_11,
  output out_12,
  output out_13,
  output out_14
);

  wire Clock_out, d_ff_1_q, d_ff_2_q, d_ff_3_q, d_ff_4_q, multiplexer_2_out, multiplexer_3_out,
       multiplexer_4_out, multiplexer_5_out, not_1_out;

  Button Clock (.out(Clock_out));
  Multiplexer multiplexer_1 (.in0(d_ff_1_q), .in1(d_ff_4_q), .out(out_10), .sel(S0), .en(not_1_out));
  not not_1 (not_1_out, S2);
  Multiplexer #(.select(2)) multiplexer_2 (
    .in0(d_ff_2_q), .in1(Data_In_for_Serial_In), .in2(in_5), .in3(in_5), .out(multiplexer_2_out),
    .sel({S1, S0}), .en(Enable));
  and and_1 (out_11, d_ff_1_q, S2);
  D_Flip_Flop d_ff_1 (.clk(Clock_out), .D(multiplexer_2_out), .Q(d_ff_1_q), .en(Enable));  // open: Qn, preset, reset
  Multiplexer #(.select(2)) multiplexer_3 (
    .in0(d_ff_3_q), .in1(d_ff_1_q), .in2(in_6), .in3(in_6), .out(multiplexer_3_out), .sel({S1, S0}),
    .en(Enable));
  and and_2 (out_12, d_ff_2_q, S2);
  D_Flip_Flop d_ff_2 (.clk(Clock_out), .D(multiplexer_3_out), .Q(d_ff_2_q), .en(Enable));  // open: Qn, preset, reset
  D_Flip_Flop d_ff_3 (.clk(Clock_out), .D(multiplexer_4_out), .Q(d_ff_3_q), .en(Enable));  // open: Qn, preset, reset
  Multiplexer #(.select(2)) multiplexer_4 (
    .in0(d_ff_4_q), .in1(d_ff_2_q), .in2(in_7), .in3(in_7), .out(multiplexer_4_out), .sel({S1, S0}),
    .en(Enable));
  and and_3 (out_13, d_ff_3_q, S2);
  Multiplexer #(.select(2)) multiplexer_5 (
    .in0(Data_In_for_Serial_In), .in1(d_ff_3_q), .in2(in_8), .in3(in_8), .out(multiplexer_5_out),
    .sel({S1, S0}), .en(Enable));
  and and_4 (out_14, d_ff_4_q, S2);
  D_Flip_Flop d_ff_4 (.clk(Clock_out), .D(multiplexer_5_out), .Q(d_ff_4_q), .en(Enable));  // open: Qn, preset, reset
endmodule
