// Logisim project Week 2 Prac.circ as structural Verilog: 1 circuit, main circuit main
module main (
  input  in_1,
  input  in_2,
  input  in_3,
  input  in_4,
  input  in_5,
  input  in_6,
  input  in_7,
  input  in_8,
  input  in_9,
  input  A3,
  input  A2,
  input  A1,
  input  A0,
  input  B3,
  input  B2,
  input  B1,
  input  B0,
  input  Cin,
  output out_19,
  output out_20,
  output out_21,
  output out_22,
  output out_23,
  output C3,
  output C2,
  output C1,
  output C0,
  output S3,
  output S2,
  output S1,
  output S0
);

  wire adder_1_cout, adder_2_cout, adder_3_cout, and_1_out, and_2_out, and_3_out, and_4_out, G0_out, G1_out,
       G2_out, G3_out, P0_out, P1_out, P2_out, P3_out;

  Adder #(.width(1)) adder_1 (.a(in_2), .b(in_3), .out(out_19), .cin(in_1), .cout(adder_1_cout));
  Adder #(.width(1)) adder_2 (.a(in_4), .b(in_5), .out(out_20), .cin(adder_1_cout), .cout(adder_2_cout));
  Adder #(.width(1)) adder_3 (.a(in_6), .b(in_7), .out(out_21), .cin(adder_2_cout), .cout(adder_3_cout));
  Adder #(.width(1)) adder_4 (.a(in_8), .b(in_9), .out(out_22), .cin(adder_3_cout), .cout(out_23));
  and G0 (G0_out, B0, A0);
  and G1 (G1_out, B1, A1);
  and G2 (G2_out, B2, A2);
  and G3 (G3_out, B3, A3);
  xor P0 (P0_out, B0, A0);
  xor P1 (P1_out, B1, A1);
  xor P2 (P2_out, B2, A2);
  xor P3 (P3_out, B3, A3);
  and and_1 (and_1_out, Cin, P0_out);
  and and_2 (and_2_out, C1, P2_out);
  and and_3 (and_3_out, P3_out, C2);
  or or_1 (C0, G0_out, and_1_out);
  and and_4 (and_4_out, C0, P1_out);
  or or_2 (C2, G2_out, and_2_out);
  or or_3 (C3, G3_out, and_3_out);
  or or_4 (C1, G1_out, and_4_out);
  xor u_S0 (S0, Cin, P0_out);
  xor u_S1 (S1, C0, P1_out);
  xor u_S2 (S2, C1, P2_out);
  xor u_S3 (S3, C2, P3_out);

  // Notes on the sheet:
  //   Week 2 Practical
  //   B - 1
  //   BT20HCS081
  //   8505854809
endmodule
